// Logisim project logisim_design.circ as structural Verilog: 1 circuit, main circuit main
module main (
  input  [15:0] A,
  input  [15:0] B
);

  Adder #(.width(16)) adder_1 ();  // open: a, b, out, cin, cout
  Subtractor #(.width(16)) subtractor_1 ();  // open: a, b, out, bin, bout
  Multiplier #(.width(16)) multiplier_1 ();  // open: a, b, out, cin, cout
  // AND_Gate and_1 is placed but not wired
  // OR_Gate or_1 is placed but not wired
  // XOR_Gate xor_1 is placed but not wired
  // NOT_Gate not_1 is placed but not wired
  Shifter #(.width(16)) shifter_1 (.\dist (4'b0001));  // open: in, out
  Shifter #(.shift("ar"), .width(16)) shifter_2 (.\dist (4'b0001));  // open: in, out
endmodule
